# Fritzing sketch Sketch (saved by Fritzing 0.9.5d)
circuit board: 8.46667cm x 5.64444cm
breadboards: 1

parts:
  RHT1 = Humidity and Temperature Sensor RHT03
  Grove1 = Grove OLED 128x96
  U1 = ESP8266 NodeMCU LoLin module
  C1 = Ceramic Capacitor [capacitance=10nF package="100 mil [THT, multilayer]"]
  R1 = Resistor [tolerance=±5% resistance=10k package=THT]
  R2 = Resistor [tolerance=±5% resistance=10k package=THT]
  S1 = Pushbutton [package="[THT]"]

nets:
  VCC: RHT1.Vcc, Grove1.VCC, U1.3V3, R1.Pin_0, R2.Pin_1, S1.Pin_1, S1.Pin_2
  N1: RHT1.Data-signal, U1.D4, R2.Pin_0
  GND: RHT1.GND_2, Grove1.GND, U1.GND, C1.1
  N2: Grove1.SDA, U1.D2
  N3: Grove1.SCL, U1.D1
  N4: U1.D5, C1.0, R1.Pin_1
  N5: S1.Pin_3, S1.Pin_4

custom parts:
  ESP8266 NodeMCU LoLin module: ESP8266 based NodeMCU
